# Fritzing sketch fz-charduindi (saved by Fritzing 0.9.3b)
circuit board: 13.3303cm x 2.88809cm
breadboards: 1

parts:
  LED13 = LED - 5mm [color="Green (555nm)" part_number=C503B-GCN-CY0C0791 current=20mA package="5 mm [THT]"]
  LED6 = LED - 5mm [color="Green (555nm)" part_number=C503B-GCN-CY0C0791 current=20mA package="5 mm [THT]"]
  LED11 = LED - 5mm [color="Green (555nm)" part_number=C503B-GCN-CY0C0791 current=20mA package="5 mm [THT]"]
  R5 = Resistor [tolerance=±5% resistance=75 package=THT]
  LED12 = LED - 5mm [color="Green (555nm)" part_number=C503B-GCN-CY0C0791 current=20mA package="5 mm [THT]"]
  LED15 = LED - 5mm [color="Green (555nm)" part_number=C503B-GCN-CY0C0791 current=20mA package="5 mm [THT]"]
  LED14 = LED - 5mm [color="Green (555nm)" part_number=C503B-GCN-CY0C0791 current=20mA package="5 mm [THT]"]
  R3 = Resistor [tolerance=±5% resistance=75 package=THT]
  LED2 = LED - 5mm [color="Green (555nm)" part_number=C503B-GCN-CY0C0791 current=20mA package="5 mm [THT]"]
  ATMEGA328p = atmega328 [package=dip]
  LED8 = LED - 5mm [color="Green (555nm)" part_number=C503B-GCN-CY0C0791 current=20mA package="5 mm [THT]"]
  LED9 = LED - 5mm [color="Green (555nm)" part_number=C503B-GCN-CY0C0791 current=20mA package="5 mm [THT]"]
  LED7 = LED - 5mm [color="Green (555nm)" part_number=C503B-GCN-CY0C0791 current=20mA package="5 mm [THT]"]
  LED18 = LED - 5mm [color="Green (555nm)" part_number=C503B-GCN-CY0C0791 current=20mA package="5 mm [THT]"]
  R4 = Resistor [tolerance=±5% resistance=75 package=THT]
  LED16 = LED - 5mm [color="Green (555nm)" part_number=C503B-GCN-CY0C0791 current=20mA package="5 mm [THT]"]
  R1 = Resistor [tolerance=±5% resistance=75 package=THT]
  LED17 = LED - 5mm [color="Green (555nm)" part_number=C503B-GCN-CY0C0791 current=20mA package="5 mm [THT]"]
  LED20 = LED - 5mm [color="Green (555nm)" part_number=C503B-GCN-CY0C0791 current=20mA package="5 mm [THT]"]
  LED5 = LED - 5mm [color="Green (555nm)" part_number=C503B-GCN-CY0C0791 current=20mA package="5 mm [THT]"]
  LED4 = LED - 5mm [color="Green (555nm)" current=0pA package="5 mm [THT]"]
  LED10 = LED - 5mm [color="Green (555nm)" part_number=C503B-GCN-CY0C0791 current=20mA package="5 mm [THT]"]
  LED3 = LED - 5mm [color="Green (555nm)" part_number=C503B-GCN-CY0C0791 current=20mA package="5 mm [THT]"]
  LED1 = LED - 5mm [color="Green (555nm)" part_number=C503B-GCN-CY0C0791 current=20mA package="5 mm [THT]"]
  LED19 = LED - 5mm [color="Green (555nm)" part_number=C503B-GCN-CY0C0791 current=20mA package="5 mm [THT]"]
  R2 = Resistor [tolerance=±5% resistance=75 package=THT]
  16_MHz = Crystal [frequency="16 Mhz" package=THT]
  ISP = AVR ISP 6 Pin [package=2x3]
  C1 = Capacitor [package=cap-pth-small2]
  C2 = Capacitor [package=cap-pth-small2]
  FTDI1 = FTDI Basic Programmer

nets:
  N1: LED13.cathode, LED15.cathode, LED14.cathode, R4.Pin_0, LED16.cathode
  charlie 5: LED13.anode, ATMEGA328p.D6_(PWM), LED9.anode, R1.Pin_1, LED17.anode, LED5.anode
  N2: LED6.cathode, LED8.cathode, LED7.cathode, LED5.cathode, R2.Pin_0
  charlie 3: LED6.anode, LED15.anode, R3.Pin_1, LED2.anode, ATMEGA328p.D4, LED20.anode
  N3: LED11.cathode, LED12.cathode, R3.Pin_0, LED9.cathode, LED10.cathode
  charlie 2: LED11.anode, ATMEGA328p.D3_(PWM), LED7.anode, R4.Pin_1, LED3.anode, LED19.anode
  N4: R5.Pin_0, LED18.cathode, LED17.cathode, LED20.cathode, LED19.cathode
  charlie 1: R5.Pin_1, LED12.anode, ATMEGA328p.D2, LED8.anode, LED16.anode, LED4.anode
  charlie 4: LED14.anode, ATMEGA328p.D5_(PWM), LED18.anode, LED10.anode, LED1.anode, R2.Pin_1
  N5: LED2.cathode, R1.Pin_0, LED4.cathode, LED3.cathode, LED1.cathode
  reset: ATMEGA328p.RESET, ISP.5
  rx: ATMEGA328p.D0_(RX), FTDI1.TXO
  tx: ATMEGA328p.D1_(TX), FTDI1.RXI
  5vcc: ATMEGA328p.VCC, ISP.2, FTDI1.POWER
  GND: ATMEGA328p.GND, ISP.6, C1.2, C2.2, FTDI1.GND
  xtal1: ATMEGA328p.XLAT1, 16_MHz.pin_0, C2.1
  xtal2: ATMEGA328p.XLAT2, 16_MHz.pin_1, C1.1
  mosi: ATMEGA328p.D11_(PWM), ISP.4
  miso: ATMEGA328p.D12, ISP.1
  sck: ATMEGA328p.D13, ISP.3

notes:
  ⏚
  Charduindicator, Charlieplexed 20-LED display with built-in Arduino Uno, 0
